# Fritzing sketch regulator r1 (saved by Fritzing 0.8.3b)
circuit board: 7.5cm x 7.5cm
breadboards: 1

parts:
  Nano = Arduino Nano (Rev3.0)
  485IC = MAX485 [package=dil08]
  R1 = Resistor [tolerance=±5% resistance=680 package=THT]
  R2 = Resistor [tolerance=±5% resistance=680 package=THT]
  485_A/B = Screw terminal - 2 pins [package=THT]
  12VIn = Screw terminal - 2 pins [package=THT]
  Pixel_PWR = Screw terminal - 2 pins [package=THT]
  Pixel = Screw terminal - 2 pins [package=THT]
  12V-5Vin = Screw terminal - 2 pins [package=THT]
  12V-5Vout = Screw terminal - 2 pins [package=THT]
  12V_Reg = Voltage Regulator - Variable [package="TO220 [THT]"]
  C2 = Electrolytic Capacitor [capacitance=10µF package="100 mil [THT, electrolytic]"]
  C1 = Electrolytic Capacitor [capacitance=1µF package="100 mil [THT, electrolytic]"]

nets:
  GND: Nano.GND, 485IC.RE, 485IC.GND, R1.Pin_1, 12VIn.pin2, 12V-5Vin.pin1, 12V_Reg.OUT, C2.-, C1.-
  N1: Nano.D2, 485IC.RO
  N2: Nano.D4, 485IC.DE
  N3: Nano.D7, 485IC.DI
  N4: Nano.D8, Pixel.pin2
  VIN: Nano.D11/MOSI, Nano.VIN, Nano.5V, 485IC.VCC, R2.Pin_1, 12V_Reg.IN, C1.+
  N5: Nano.D12/MISO, Nano.D13/SCK, Pixel.pin1
  N6: 485IC.A, R2.Pin_0, 485_A/B.pin1
  N7: 485IC.B, R1.Pin_0, 485_A/B.pin2
  N8: 12VIn.pin1, 12V-5Vin.pin2, 12V_Reg.ADJ, C2.+
  N9: Pixel_PWR.pin1, 12V-5Vout.pin1
  N10: Pixel_PWR.pin2, 12V-5Vout.pin2
