# Fritzing sketch HMTL Module v1 (saved by Fritzing 0.8.3b)
breadboards: 1

parts:
  Nano = Arduino Nano (Rev3.0)
  485IC = MAX485 [package=dil08]
  R1 = Resistor [tolerance=±5% resistance=680 package=THT]
  R2 = Resistor [tolerance=±5% resistance=680 package=THT]
  485_A/B = Screw terminal - 2 pins [package=THT]
  5VIn = Screw terminal - 2 pins [package=THT]
  Pixel_PWR = Screw terminal - 2 pins [package=THT]
  Pixel = Screw terminal - 2 pins [package=THT]
  U3 = Voltage Regulator - Variable [package="TO220 [THT]"]
  C1 = Electrolytic Capacitor [capacitance=1µF package="100 mil [THT, electrolytic]"]
  C2 = Electrolytic Capacitor [capacitance=10µF package="100 mil [THT, electrolytic]"]
  12V_in = Screw terminal - 2 pins [package=THT]
  5V_out = Screw terminal - 2 pins [package=THT]

nets:
  GND: Nano.GND, 485IC.RE, 485IC.GND, R1.Pin_1, 5VIn.pin2, U3.OUT, C1.-, C2.-, 12V_in.pin1
  N1: Nano.D2, 485IC.DI
  N2: Nano.D4, 485IC.DE
  N3: Nano.D7, 485IC.RO
  N4: Nano.D8, Pixel.pin2
  VIN: Nano.D11/MOSI, Nano.VIN, Nano.5V, 485IC.VCC, R2.Pin_1, U3.IN, C1.+
  N5: Nano.D12/MISO, Nano.D13/SCK, Pixel.pin1
  N6: 485IC.A, R2.Pin_0, 485_A/B.pin2
  N7: 485IC.B, R1.Pin_0, 485_A/B.pin1
  N8: 5VIn.pin1, U3.ADJ, C2.+, 12V_in.pin2
  N9: Pixel_PWR.pin1, 5V_out.pin1
  N10: Pixel_PWR.pin2, 5V_out.pin2
