# Fritzing sketch regulator r3 (saved by Fritzing 0.8.3b)
circuit board: 7cm x 5cm
breadboards: 1

parts:
  Nano = Arduino Nano (Rev3.0)
  485IC = MAX485 [package=dil08]
  R1 = Resistor [tolerance=±5% resistance=680 package=THT]
  R2 = Resistor [tolerance=±5% resistance=680 package=THT]
  485_A/B = Screw terminal - 2 pins [package=THT]
  12VIn = Screw terminal - 2 pins [package=THT]
  PixPWR = Screw terminal - 2 pins [package=THT]
  Pixel = Screw terminal - 2 pins [package=THT]
  12V-5Vin = Screw terminal - 2 pins [package=THT]
  12V-5Vout = Screw terminal - 2 pins [package=THT]
  1uf = Electrolytic Capacitor [capacitance=1µF package="100 mil [THT, electrolytic]"]
  10uf = Electrolytic Capacitor [capacitance=10µF package="100 mil [THT, electrolytic]"]
  12V_Reg = Voltage Regulator - Variable [package="TO220 [THT]"]
  68 = Resistor [tolerance=±5% resistance=68 package=THT]
  RGB = RGB LED (com. cathode, rbg) [package="5 mm [THT]"]
  DBG = LED - 5mm [color="White (6500K)" package="5 mm [THT]"]
  R3 = Resistor [tolerance=±5% resistance=150 package=THT]
  R4 = Resistor [tolerance=±5% resistance=100 package=THT]
  R5 = Resistor [tolerance=±5% resistance=100 package=THT]

nets:
  GND: Nano.GND, 485IC.RE, 485IC.GND, R1.Pin_1, 12VIn.pin2, 12V-5Vin.pin1, 1uf.-, 10uf.-, 12V_Reg.OUT, RGB.common_cathode, DBG.cathode
  N1: Nano.D2, 485IC.RO
  N2: Nano.D4, 485IC.DE
  N3: Nano.D7, 485IC.DI
  N4: Nano.D8, Pixel.pin2
  N5: Nano.D9, R3.Pin_0
  N6: Nano.D10, R4.Pin_0
  VIN: Nano.D11/MOSI, Nano.VIN, Nano.5V, 485IC.VCC, R2.Pin_1, 1uf.+, 12V_Reg.IN, R5.Pin_0
  N7: Nano.D12/MISO, Nano.D13/SCK, Pixel.pin1, 68.Pin_1
  N8: 485IC.A, R2.Pin_0, 485_A/B.pin1
  N9: 485IC.B, R1.Pin_0, 485_A/B.pin2
  N10: 12VIn.pin1, 12V-5Vin.pin2, 10uf.+, 12V_Reg.ADJ
  N11: PixPWR.pin1, 12V-5Vout.pin1
  N12: PixPWR.pin2, 12V-5Vout.pin2
  N13: 68.Pin_0, DBG.anode
  N14: RGB.red_anode, R3.Pin_1
  N15: RGB.blue_anode, R4.Pin_1
  N16: RGB.green_anode, R5.Pin_1
