# Fritzing sketch regulator r4 (saved by Fritzing 0.8.3b)
circuit board: 7cm x 6.22859cm
breadboards: 1

parts:
  Nano = Arduino Nano (Rev3.0)
  485IC = MAX485 [package=dil08]
  680 = Resistor [tolerance=±5% resistance=680 package=THT]
  680_2 = Resistor [tolerance=±5% resistance=680 package=THT]
  485_A/B = Screw terminal - 2 pins [package=THT]
  12VIn = Screw terminal - 2 pins [package=THT]
  PixPWR = Screw terminal - 2 pins [package=THT]
  Pixel = Screw terminal - 2 pins [package=THT]
  12V-5Vin = Screw terminal - 2 pins [package=THT]
  12V-5Vout = Screw terminal - 2 pins [package=THT]
  1uf = Electrolytic Capacitor [capacitance=1µF package="100 mil [THT, electrolytic]"]
  10uf = Electrolytic Capacitor [capacitance=10µF package="100 mil [THT, electrolytic]"]
  12V_Reg = Voltage Regulator - Variable [package="TO220 [THT]"]
  D2_D3 = Screw terminal - 2 pins [package=THT]
  D6_D9 = Screw terminal - 2 pins [package=THT]
  A1_A0 = Screw terminal - 2 pins [package=THT]
  5V_GND = Screw terminal - 2 pins [package=THT]
  3V_GND = Screw terminal - 2 pins [package=THT]
  A5_A4 = Screw terminal - 2 pins [package=THT]
  RGB = RGB LED (com. cathode, rbg) [package="5 mm [THT]"]
  R4 = Resistor [tolerance=±5% resistance=150 package=THT]
  R5 = Resistor [tolerance=±5% resistance=100 package=THT]
  R6 = Resistor [tolerance=±5% resistance=100 package=THT]

nets:
  GND: Nano.GND, 485IC.RE, 485IC.GND, 680.Pin_1, 12VIn.pin1, 12V-5Vin.pin1, 1uf.-, 10uf.-, 12V_Reg.OUT, 5V_GND.pin2, 3V_GND.pin2, RGB.common_cathode
  N1: Nano.D2, D2_D3.pin1
  N2: Nano.D3, D2_D3.pin2
  N3: Nano.D4, 485IC.RO
  N4: Nano.D5, 485IC.DE
  N5: Nano.D6, D6_D9.pin1
  N6: Nano.D7, 485IC.DI
  N7: Nano.D8, Pixel.pin2
  N8: Nano.D9, D6_D9.pin2
  N9: Nano.D10, R4.Pin_0
  VIN: Nano.D11/MOSI, Nano.VIN, Nano.5V, 485IC.VCC, 680_2.Pin_1, 1uf.+, 12V_Reg.IN, 5V_GND.pin1, R5.Pin_0
  N10: Nano.D12/MISO, Nano.D13/SCK, Pixel.pin1, R6.Pin_0
  N11: Nano.A5, A5_A4.pin1
  N12: Nano.A4, A5_A4.pin2
  N13: Nano.A1, A1_A0.pin1
  N14: Nano.A0, A1_A0.pin2
  N15: Nano.3V3, 3V_GND.pin1
  N16: 485IC.A, 680_2.Pin_0, 485_A/B.pin1
  N17: 485IC.B, 680.Pin_0, 485_A/B.pin2
  N18: 12VIn.pin2, 12V-5Vin.pin2, 10uf.+, 12V_Reg.ADJ
  N19: PixPWR.pin1, 12V-5Vout.pin1
  N20: PixPWR.pin2, 12V-5Vout.pin2
  N21: RGB.red_anode, R4.Pin_1
  N22: RGB.blue_anode, R5.Pin_1
  N23: RGB.green_anode, R6.Pin_1
