# Fritzing sketch regulator r7 (saved by Fritzing 0.8.3b)
circuit board: 7cm x 6.22859cm
breadboards: 1

parts:
  485IC = MAX485 [package=dil08]
  680 = Resistor [tolerance=±5% resistance=680 package=THT]
  680_2 = Resistor [tolerance=±5% resistance=680 package=THT]
  485_A/B = Screw terminal - 2 pins [package=THT]
  12VIn = Screw terminal - 2 pins [package=THT]
  AuxVout = Screw terminal - 2 pins [package=THT]
  D8_D12 = Screw terminal - 2 pins [package=THT]
  12Vout = Screw terminal - 2 pins [package=THT]
  AuxVin = Screw terminal - 2 pins [package=THT]
  1uf = Electrolytic Capacitor [capacitance=1µF package="100 mil [THT, electrolytic]"]
  10uf = Electrolytic Capacitor [capacitance=10µF package="100 mil [THT, electrolytic]"]
  12V_Reg = Voltage Regulator - Variable [package="TO220 [THT]"]
  D3_D5 = Screw terminal - 2 pins [package=THT]
  D6_D9 = Screw terminal - 2 pins [package=THT]
  A1_A0 = Screw terminal - 2 pins [package=THT]
  5Vout = Screw terminal - 2 pins [package=THT]
  3Vout = Screw terminal - 2 pins [package=THT]
  A5_A4 = Screw terminal - 2 pins [package=THT]
  150 = Resistor [tolerance=±5% resistance=150 package=THT]
  100 = Resistor [tolerance=±5% resistance=100 package=THT]
  1N4001 = Diode [package=diode-1n4001]
  Nano = Arduino Nano (Rev3.0)
  100_2 = Resistor [tolerance=±5% resistance=100 package=THT]
  RGB = Super Flux RGB LED (com. cathode)
  ARef = male pin header, 2 pins [form="♂ (male)"]
  A3_A2 = male pin header, 2 pins [form="♂ (male)"]
  A7_A6 = male pin header, 2 pins [form="♂ (male)"]
  D1_D0 = male pin header, 2 pins [form="♂ (male)"]
  D13 = male pin header, 1 pin [form="♂ (male)"]
  D10_D11 = Screw terminal - 2 pins [package=THT]

nets:
  N1: 485IC.RO, Nano.D4
  GND: 485IC.RE, 485IC.GND, 680.Pin_1, 12VIn.pin1, 12Vout.pin1, 1uf.-, 10uf.-, 12V_Reg.OUT, 5Vout.pin2, 3Vout.pin2, Nano.GND, RGB.common_cathode
  N2: 485IC.DE, Nano.D2
  N3: 485IC.DI, Nano.D7
  N4: 485IC.A, 680_2.Pin_0, 485_A/B.pin1
  N5: 485IC.B, 680.Pin_0, 485_A/B.pin2
  VCC: 485IC.VCC, 680_2.Pin_1, 5Vout.pin1, 1N4001.C, Nano.VIN, Nano.5V
  N6: 12VIn.pin2, 12Vout.pin2, 10uf.+, 12V_Reg.ADJ
  N7: AuxVout.pin1, AuxVin.pin1
  N8: AuxVout.pin2, AuxVin.pin2
  N9: D8_D12.pin1, Nano.D12/MISO
  N10: D8_D12.pin2, Nano.D8
  N11: 1uf.+, 12V_Reg.IN, 1N4001.A
  N12: D3_D5.pin1, Nano.D3
  N13: D3_D5.pin2, Nano.D5
  N14: D6_D9.pin1, Nano.D6
  N15: D6_D9.pin2, Nano.D9
  N16: A1_A0.pin1, Nano.A1
  N17: A1_A0.pin2, Nano.A0
  N18: 3Vout.pin1, Nano.3V3, ARef.pin1
  N19: A5_A4.pin1, Nano.A5
  N20: A5_A4.pin2, Nano.A4
  N21: 150.Pin_0, Nano.D10, D10_D11.pin2
  N22: 150.Pin_1, RGB.red_anode
  N23: 100.Pin_0, Nano.D11/MOSI, D10_D11.pin1
  N24: 100.Pin_1, RGB.green_anode
  N25: Nano.D1/TX, D1_D0.pin2
  N26: Nano.D0/RX, D1_D0.pin1
  N27: Nano.A7, A7_A6.pin2
  N28: Nano.A6, A7_A6.pin1
  N29: Nano.A3, A3_A2.pin2
  N30: Nano.A2, A3_A2.pin1
  N31: Nano.AREF, ARef.pin2
  N32: Nano.D13/SCK, 100_2.Pin_0, D13.pin1
  N33: 100_2.Pin_1, RGB.blue_anode

notes:
  HMTL v1r5
  + -
  i2c
