# Fritzing sketch regulator r9 (saved by Fritzing 0.8.3b)
circuit board: 7cm x 6.22859cm
breadboards: 1

parts:
  485IC = MAX485 [package=dil08]
  680 = Resistor [tolerance=±5% resistance=680 package=THT]
  680_2 = Resistor [tolerance=±5% resistance=680 package=THT]
  1uf = Electrolytic Capacitor [capacitance=1µF package="100 mil [THT, electrolytic]"]
  10uf = Electrolytic Capacitor [capacitance=10µF package="100 mil [THT, electrolytic]"]
  12V_Reg = Voltage Regulator - Variable [package="TO220 [THT]"]
  100 = Resistor [tolerance=±5% resistance=100 package=THT]
  1N4001 = Diode [package=diode-1n4001]
  Nano = Arduino Nano (Rev3.0)
  150 = Resistor [tolerance=±5% resistance=150 package=THT]
  RGB = Super Flux RGB LED (com. cathode)
  ARef = male pin header, 2 pins [form="♂ (male)"]
  A3_A2 = male pin header, 2 pins [form="♂ (male)"]
  A7_A6 = male pin header, 2 pins [form="♂ (male)"]
  D1_D0 = male pin header, 2 pins [form="♂ (male)"]
  D13 = male pin header, 1 pin [form="♂ (male)"]
  100_2 = Resistor [tolerance=±5% resistance=100 package=THT]
  5Vout = Screw terminal - 2 pins [package=THT]
  3Vout = screw terminal, 2 pins
  A5_A4 = screw terminal, 2 pins
  A1_A0 = screw terminal, 2 pins
  D3_D5 = screw terminal, 2 pins
  D6_D9 = screw terminal, 2 pins
  485_A/B = screw terminal, 2 pins
  12VIn = screw terminal, 2 pins
  12Vout = screw terminal, 2 pins
  AuxVout = screw terminal, 2 pins
  D8_D12 = screw terminal, 2 pins
  D10_D11 = screw terminal, 2 pins
  AuxVin = screw terminal, 2 pins

nets:
  N1: 485IC.RO, Nano.D4
  GND: 485IC.RE, 485IC.GND, 680.Pin_1, 1uf.-, 10uf.-, 12V_Reg.OUT, Nano.GND, RGB.common_cathode, 5Vout.pin2, 3Vout.pin2, 12VIn.pin1, 12Vout.pin1
  N2: 485IC.DE, Nano.D2
  N3: 485IC.DI, Nano.D7
  N4: 485IC.A, 680_2.Pin_0, 485_A/B.pin1
  N5: 485IC.B, 680.Pin_0, 485_A/B.pin2
  VCC: 485IC.VCC, 680_2.Pin_1, 1N4001.C, Nano.VIN, Nano.5V, 5Vout.pin1
  N6: 1uf.+, 12V_Reg.IN, 1N4001.A
  N7: 10uf.+, 12V_Reg.ADJ, 12VIn.pin2, 12Vout.pin2
  N8: 100.Pin_0, Nano.D10, D10_D11.pin2
  N9: 100.Pin_1, RGB.red_anode
  N10: Nano.D1/TX, D1_D0.pin2
  N11: Nano.D0/RX, D1_D0.pin1
  N12: Nano.D3, D3_D5.pin1
  N13: Nano.D5, D3_D5.pin2
  N14: Nano.D6, D6_D9.pin1
  N15: Nano.D8, D8_D12.pin2
  N16: Nano.D9, D6_D9.pin2
  N17: Nano.D11/MOSI, 100_2.Pin_0, D10_D11.pin1
  N18: Nano.D12/MISO, D8_D12.pin1
  N19: Nano.A7, A7_A6.pin2
  N20: Nano.A6, A7_A6.pin1
  N21: Nano.A5, A5_A4.pin1
  N22: Nano.A4, A5_A4.pin2
  N23: Nano.A3, A3_A2.pin2
  N24: Nano.A2, A3_A2.pin1
  N25: Nano.A1, A1_A0.pin1
  N26: Nano.A0, A1_A0.pin2
  N27: Nano.AREF, ARef.pin2
  N28: Nano.3V3, ARef.pin1, 3Vout.pin1
  N29: Nano.D13/SCK, 150.Pin_0, D13.pin1
  N30: 150.Pin_1, RGB.blue_anode
  N31: RGB.green_anode, 100_2.Pin_1
  N32: AuxVout.pin1, AuxVin.pin1
  N33: AuxVout.pin2, AuxVin.pin2

notes:
  HMTL v1r9
  + -
  i2c
